# Fritzing sketch Wiring diagram (saved by Fritzing 0.9.4)
breadboards: 1

parts:
  Part1 = Breakout Board for Electret Microphone
  Bela1 = Bela
  SparkFun1 = SoftPot Membrane Potentiometer - 50mm [part_number=SEN-08680]
  Part2 = Triple Axis Accelerometer Breakout - ADXL335
  S1 = Momentary Switch [package=ksa_sealed_tac_switch]
  S2 = Momentary Switch [package=ksa_sealed_tac_switch]
  S3 = Momentary Switch [package=ksa_sealed_tac_switch]
  R1 = Resistor [tolerance=±5% resistance=1k package="0603 [SMD]"]
  R2 = Resistor [tolerance=±5% resistance=1k package="0603 [SMD]"]
  R3 = Resistor [tolerance=±5% resistance=1k package="0603 [SMD]"]

nets:
  N1: Part1.VCC, Bela1.AUDIOIN_L
  GND: Part1.GND, Bela1.P9_01_GND, SparkFun1.leg1, Part2.GND, R1.Pin_0, R2.Pin_0, R3.Pin_0
  N2: Part1.AUD, Bela1.P9_03_3.3V, SparkFun1.leg2, Part2.VCC, S1.3, S2.3, S3.3
  N3: Bela1.P8_08_D1, S3.1, R3.Pin_1
  N4: Bela1.P8_10_D3, S2.1, R2.Pin_1
  N5: Bela1.P8_12_D5, S1.1, R1.Pin_1
  N6: Bela1.AIN_3, Part2.ZOUT
  N7: Bela1.AIN_2, Part2.YOUT
  N8: Bela1.AIN_1, Part2.XOUT
  N9: Bela1.AIN_0, SparkFun1.wiper

custom parts:
  Bela: A Fritzing part for Bela
  SoftPot Membrane Potentiometer - 50mm: These are very thin variable potentiometers. By pressing down on various parts of the strip, the resistance linearly changes from 100Ohms to 10,000Ohms allowing the user to very accurately calculate the relative position on the strip. Can be used as an accurate positional indicator for CNC head positioning, variable user input (volume level input for example), straight user input (multiple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
